# Fritzing sketch Közlekedési_Lámpa (saved by Fritzing 0.9.9b)
breadboards: 1

parts:
  Mod1 = Raspberry Pi 4B
  Gyalog_Zöld = LED - 5mm [color="Red (633nm)" current=0.030 package="5 mm [THT]"]
  Gyalog_Piros = LED - 5mm [color="Red (633nm)" current=0.030 package="5 mm [THT]"]
  R1 = Resistor [tolerance=±5% power=0.25 resistance=3.3k package=THT]
  R2 = Resistor [tolerance=±5% power=0.25 resistance=3.3k package=THT]
  R3 = Resistor [tolerance=±5% power=0.25 resistance=3.3k package=THT]
  Köz_Piros = LED - 5mm [color="Red (633nm)" current=0.030 package="5 mm [THT]"]
  Köz_Sárga = LED - 5mm [color="Red (633nm)" current=0.030 package="5 mm [THT]"]
  Köz_Zöld = LED - 5mm [color="Red (633nm)" current=0.030 package="5 mm [THT]"]
  R4 = Resistor [tolerance=±5% power=0.25 resistance=3.3k package=THT]
  R5 = Resistor [tolerance=±5% power=0.25 resistance=3.3k package=THT]

nets:
  N1: Mod1.GPIO13, R1.Pin_1
  N2: Mod1.GPIO16, R4.Pin_1
  N3: Mod1.GPIO26, R2.Pin_1
  N4: Mod1.GPIO20, R5.Pin_1
  N5: Mod1.GND, Gyalog_Zöld.cathode, Gyalog_Piros.cathode, Köz_Piros.cathode, Köz_Sárga.cathode, Köz_Zöld.cathode
  N6: Mod1.GPIO21, R3.Pin_1
  N7: Gyalog_Zöld.anode, R1.Pin_0
  N8: Gyalog_Piros.anode, R2.Pin_0
  N9: R3.Pin_0, Köz_Piros.anode
  N10: Köz_Sárga.anode, R5.Pin_0
  N11: Köz_Zöld.anode, R4.Pin_0
